# Fritzing sketch wiring-diagram (saved by Fritzing 0.9.2b)
breadboards: 1

parts:
  Transceiver1 = nRF24L01 [package=module]
  Mod2 = KY-023 Dual Axis Joystick Module [package="Breakout board"]
  Parte1 = Arduino Uno (Rev3) - ICSP
  Left_Joystick = KY-023 Dual Axis Joystick Module [package="Breakout board"]

nets:
  GND: Transceiver1.GND, Mod2.GND, Parte1.GND, Left_Joystick.GND
  VCC: Transceiver1.VCC, Parte1.3V3
  N1: Transceiver1.CE, Parte1.D9_PWM
  N2: Transceiver1.CSN, Parte1.D10_PWM/SS
  N3: Transceiver1.SCK, Parte1.D13/SCK
  N4: Transceiver1.MOSI, Parte1.D11_PWM/MOSI
  N5: Transceiver1.MISO, Parte1.D12/MISO
  +5V: Mod2.+5V, Parte1.5V, Left_Joystick.+5V
  N6: Mod2.VRx, Parte1.A2
  N7: Mod2.VRy, Parte1.A3
  N8: Mod2.SW, Parte1.D4
  N9: Parte1.A0, Left_Joystick.VRx
  N10: Parte1.A1, Left_Joystick.VRy
  N11: Parte1.D2, Left_Joystick.SW

custom parts:
  nRF24L01: nRF24L01 module
  KY-023 Dual Axis Joystick Module: KY-023 Dual-Axis Joystick Module.
